// Logisim project Project 7.circ as structural Verilog: 1 circuit, main circuit main
module main (
  input  Reset,
  output [3:0] out_2,
  output [7:0] out_3
);

  wire and_3_out, and_5_out, Clock, Decode_enable, decoder_1_out2, decoder_1_out6, decoder_1_out7,
       decoder_1_out8, decoder_1_out10, decoder_1_out11, decoder_2_out4, decoder_2_out5, decoder_2_out6,
       decoder_2_out7, decoder_2_out8, Execute_enable, Load_to_tmp, not_1_out, not_2_out, not_3_out,
       or_1_out, or_3_out, or_4_out, pull_resistor_1_node, pull_resistor_2_node, pull_resistor_3_node,
       pull_resistor_4_node, pull_resistor_5_node, pull_resistor_10_node, pull_resistor_11_node,
       pull_resistor_12_node, pull_resistor_13_node, Select_accumulator, Stop, Store_from_tmp;
  wire [1:0] counter_1_q;
  wire [3:0] bitselector_1_out, counter_2_q;
  wire [7:0] accumulator_in, accumulator_out, adder_1_out, Instruction, negator_1_out, pull_resistor_23_node,
       pull_resistor_25_node, ram_1_data, shifter_1_out, shifter_2_out, shifter_3_out, shifter_4_out,
       shifter_5_out, subtractor_1_out, tmp_in, tmp_out, transistor_3_out, transistor_5_out,
       transistor_6_out, transistor_8_out, transistor_10_out, transistor_11_out, transistor_12_out,
       transistor_13_out, Value;

  Clock clock_1 (.out(Clock));
  Counter #(.width(2), .max('h2)) counter_1 (.Q(counter_1_q), .clk(Clock), .clr(Reset));  // open: load, D, count, carry
  and and_1 (Execute_enable, counter_1_q[1], not_1_out);
  not not_1 (not_1_out, counter_1_q[0]);
  not not_2 (not_2_out, counter_1_q[1]);
  and and_2 (Decode_enable, not_2_out, counter_1_q[0]);
  and and_3 (and_3_out, not_1_out, not_2_out);
  Pull_Resistor pull_resistor_1 (.node(pull_resistor_1_node));
  Pull_Resistor pull_resistor_2 (.node(pull_resistor_2_node));
  Pull_Resistor pull_resistor_3 (.node(pull_resistor_3_node));
  Pull_Resistor pull_resistor_4 (.node(pull_resistor_4_node));
  Pull_Resistor pull_resistor_5 (.node(pull_resistor_5_node));
  Decoder #(.select(4)) decoder_1 (
    .out0(pull_resistor_1_node), .out1(pull_resistor_2_node), .out2(decoder_1_out2),
    .out3(pull_resistor_3_node), .out4(pull_resistor_5_node), .out5(pull_resistor_4_node),
    .out6(decoder_1_out6), .out7(decoder_1_out7), .out8(decoder_1_out8), .out9(Select_accumulator),
    .out10(decoder_1_out10), .out11(decoder_1_out11), .sel(Instruction[7:4]), .en(Decode_enable));  // open: out12, out13, out14, out15
  assign out_3 = Instruction & 8'h7;  // AND_Gate and_4, 8 bits wide
  Register u_Instruction (.D(tmp_in), .en(and_3_out), .Q(Instruction), .clk(Clock), .clr(Reset));
  Pull_Resistor pull_resistor_6 (.node(Select_accumulator));
  Pull_Resistor pull_resistor_7 (.node(decoder_1_out6));
  Pull_Resistor pull_resistor_8 (.node(decoder_1_out8));
  Pull_Resistor pull_resistor_9 (.node(decoder_1_out7));
  and and_5 (and_5_out, ~Stop, Execute_enable);  // AND_Gate
  or or_1 (or_1_out, pull_resistor_3_node, pull_resistor_5_node, pull_resistor_4_node, decoder_1_out6, decoder_1_out7);
  Transistor #(.\type ("n"), .width(8)) transistor_1 (.in(out_3), .out(Value), .gate(or_1_out));
  Counter #(.width(4), .max('hf)) counter_2 (
    .count(and_5_out), .Q(counter_2_q), .clk(Clock), .clr(Reset));  // open: load, D, carry
  or or_2 (Load_to_tmp, pull_resistor_1_node, pull_resistor_2_node, decoder_1_out8, Select_accumulator);
  Transistor #(.\type ("n"), .width(4)) transistor_2 (.in(Instruction[3:0]), .out(out_2), .gate(Load_to_tmp));
  not not_3 (not_3_out, and_3_out);
  BitSelector #(.group(4)) bitselector_1 (.in({out_2, counter_2_q}), .out(bitselector_1_out), .sel(not_3_out));
  Register register_1 (.D(accumulator_in), .en(Execute_enable), .Q(accumulator_out), .clk(Clock), .clr(Reset));
  RAM #(.addrWidth(4), .bus("separate")) ram_1 (
    .addr(bitselector_1_out), .din(tmp_out), .data(ram_1_data), .str(Store_from_tmp), .clk(Clock),
    .ld(or_3_out));  // open: sel, clr
  or or_3 (or_3_out, and_3_out, Load_to_tmp);
  Transistor #(.\type ("n"), .width(8)) transistor_3 (.in(tmp_in), .out(transistor_3_out), .gate(Load_to_tmp));
  Transistor #(.width(8)) transistor_4 (.in(Value), .out(transistor_3_out), .gate(Load_to_tmp));
  Register register_2 (.D(transistor_3_out), .en(Decode_enable), .Q(tmp_out), .clk(Clock), .clr(Reset));
  BitSelector #(.width(16), .group(8)) bitselector_2 (
    .in({accumulator_out, ram_1_data}), .out(tmp_in), .sel(Select_accumulator));
  Pull_Resistor pull_resistor_10 (.node(pull_resistor_10_node));
  Pull_Resistor pull_resistor_11 (.node(pull_resistor_11_node));
  Pull_Resistor pull_resistor_12 (.node(pull_resistor_12_node));
  Pull_Resistor pull_resistor_13 (.node(pull_resistor_13_node));
  Decoder #(.select(4)) decoder_2 (
    .out0(pull_resistor_11_node), .out1(pull_resistor_13_node), .out2(pull_resistor_10_node),
    .out3(pull_resistor_12_node), .out4(decoder_2_out4), .out5(decoder_2_out5), .out6(decoder_2_out6),
    .out7(decoder_2_out7), .out8(decoder_2_out8), .out9(Store_from_tmp), .out11(Stop),
    .sel(Instruction[7:4]), .en(Execute_enable));  // open: out10, out12, out13, out14, out15
  Pull_Resistor pull_resistor_14 (.node(Store_from_tmp));
  Pull_Resistor pull_resistor_15 (.node(Stop));
  Pull_Resistor pull_resistor_16 (.node(decoder_2_out4));
  Pull_Resistor pull_resistor_17 (.node(decoder_2_out7));
  Pull_Resistor pull_resistor_18 (.node(decoder_2_out8));
  Pull_Resistor pull_resistor_19 (.node(decoder_2_out5));
  Pull_Resistor pull_resistor_20 (.node(decoder_2_out6));
  or or_4 (or_4_out, decoder_2_out8, Store_from_tmp);
  Adder adder_1 (.a(accumulator_out), .b(tmp_out), .out(adder_1_out));  // open: cin, cout
  Transistor #(.\type ("n"), .width(8)) transistor_5 (
    .in(adder_1_out), .out(transistor_5_out), .gate(pull_resistor_11_node));
  Pull_Resistor pull_resistor_21 (.node(transistor_5_out));
  Subtractor subtractor_1 (.a(accumulator_out), .b(tmp_out), .out(subtractor_1_out));  // open: bin, bout
  Transistor #(.\type ("n"), .width(8)) transistor_6 (
    .in(subtractor_1_out), .out(transistor_6_out), .gate(pull_resistor_13_node));
  Pull_Resistor pull_resistor_22 (.node(transistor_6_out));
  Pull_Resistor pull_resistor_23 (.node(pull_resistor_23_node));
  Negator negator_1 (.in(accumulator_out), .out(negator_1_out));
  Transistor #(.\type ("n"), .width(8)) transistor_7 (
    .in(negator_1_out), .out(pull_resistor_23_node), .gate(pull_resistor_10_node));
  Transistor #(.\type ("n"), .width(8)) transistor_8 (
    .in(shifter_1_out), .out(transistor_8_out), .gate(pull_resistor_12_node));
  Pull_Resistor pull_resistor_24 (.node(transistor_8_out));
  Shifter shifter_1 (.in(accumulator_out), .\dist (tmp_out[2:0]), .out(shifter_1_out));
  Pull_Resistor pull_resistor_25 (.node(pull_resistor_25_node));
  Transistor #(.\type ("n"), .width(8)) transistor_9 (
    .in(shifter_2_out), .out(pull_resistor_25_node), .gate(decoder_2_out4));
  Shifter #(.shift("lr")) shifter_2 (.in(accumulator_out), .\dist (tmp_out[2:0]), .out(shifter_2_out));
  Shifter #(.shift("ar")) shifter_3 (.in(accumulator_out), .\dist (tmp_out[2:0]), .out(shifter_3_out));
  Transistor #(.\type ("n"), .width(8)) transistor_10 (
    .in(shifter_3_out), .out(transistor_10_out), .gate(decoder_2_out5));
  Pull_Resistor pull_resistor_26 (.node(transistor_10_out));
  Transistor #(.\type ("n"), .width(8)) transistor_11 (
    .in(shifter_4_out), .out(transistor_11_out), .gate(decoder_2_out6));
  Shifter #(.shift("rl")) shifter_4 (.in(accumulator_out), .\dist (tmp_out[2:0]), .out(shifter_4_out));
  Pull_Resistor pull_resistor_27 (.node(transistor_11_out));
  Transistor #(.\type ("n"), .width(8)) transistor_12 (
    .in(shifter_5_out), .out(transistor_12_out), .gate(decoder_2_out7));
  Pull_Resistor pull_resistor_28 (.node(transistor_12_out));
  Shifter #(.shift("rr")) shifter_5 (.in(accumulator_out), .\dist (tmp_out[2:0]), .out(shifter_5_out));
  Transistor #(.\type ("n"), .width(8)) transistor_13 (.in(tmp_out), .out(transistor_13_out), .gate(or_4_out));
  Pull_Resistor pull_resistor_29 (.node(transistor_13_out));
  Transistor #(.\type ("n"), .width(4)) transistor_14 (.in(Instruction[3:0]), .out(out_2), .gate(Store_from_tmp));
  assign accumulator_in = transistor_5_out | transistor_6_out | pull_resistor_23_node | transistor_8_out | transistor_13_out | pull_resistor_25_node | transistor_10_out | transistor_11_out | transistor_12_out;  // OR_Gate or_5, 8 bits wide

  // Other names for the same wires on the sheet: Addr[3:0] = out_2

  // Notes on the sheet:
  //   Decode
  //   Fetch
  //   Accumulator
  //   Tmp Reg
  //   Load to Instruction register or accumulator
  //   Execute
endmodule
